// Logisim project ETFStudent.circ as structural Verilog: 6 circuits, main circuit REG32_LD
module REG32_LD (
  input  [31:0] I15__0,
  input  LD,
  input  mr,
  input  CLK,
  output [31:0] A15__0
);

  // REG16_LD reg16_ld_1: pin names not known; wires that end beside it: CLK, mr, I15__0[31:16], A15__0[31:16], LD
  // REG16_LD reg16_ld_2: pin names not known; wires that end beside it: CLK, mr, I15__0[15:0], A15__0[15:0], LD

  // Notes on the sheet:
  //   __
endmodule

module KMADR (
  input  immed,
  input  memdir,
  input  memind,
  input  regind,
  input  preincr,
  input  postdec,
  input  regdir,
  output [4:0] Adr4__0
);

  assign Adr4__0 = immed ? 5'b00010 : 5'bz;  // Controlled_Buffer controlled_buffer_1
  assign Adr4__0 = memdir ? 5'b00011 : 5'bz;  // Controlled_Buffer controlled_buffer_2
  assign Adr4__0 = memind ? 5'b00100 : 5'bz;  // Controlled_Buffer controlled_buffer_3
  assign Adr4__0 = regind ? 5'b01010 : 5'bz;  // Controlled_Buffer controlled_buffer_4
  assign Adr4__0 = preincr ? 5'b01011 : 5'bz;  // Controlled_Buffer controlled_buffer_5
  assign Adr4__0 = postdec ? 5'b01111 : 5'bz;  // Controlled_Buffer controlled_buffer_6
  assign Adr4__0 = regdir ? 5'b10011 : 5'bz;  // Controlled_Buffer controlled_buffer_7
endmodule

module KMOPR (
  input  STRFIND,
  input  PUSHPSW,
  input  LD,
  input  ST,
  input  ADD,
  input  DEC,
  input  OR,
  input  BGREU,
  input  BLSSU,
  input  BLEQU,
  input  JGRT,
  input  JLEQ,
  input  JMP,
  input  JSR,
  input  RTI,
  input  POPPSW,
  input  RTS,
  input  ROR,
  input  RORC,
  input  STIVTP,
  input  HALT,
  output [6:0] Adr6__0
);

  assign Adr6__0 = LD ? 7'b0000010 : 7'bz;  // Controlled_Buffer controlled_buffer_1
  assign Adr6__0 = ST ? 7'b0000100 : 7'bz;  // Controlled_Buffer controlled_buffer_2
  assign Adr6__0 = ADD ? 7'b0000101 : 7'bz;  // Controlled_Buffer controlled_buffer_3
  assign Adr6__0 = DEC ? 7'b0000111 : 7'bz;  // Controlled_Buffer controlled_buffer_4
  assign Adr6__0 = STRFIND ? 7'b0010001 : 7'bz;  // Controlled_Buffer controlled_buffer_5
  assign Adr6__0 = OR ? 7'b0001111 : 7'bz;  // Controlled_Buffer controlled_buffer_6
  assign Adr6__0 = BGREU ? 7'b0010110 : 7'bz;  // Controlled_Buffer controlled_buffer_7
  assign Adr6__0 = BLSSU ? 7'b0010110 : 7'bz;  // Controlled_Buffer controlled_buffer_8
  assign Adr6__0 = BLEQU ? 7'b0010110 : 7'bz;  // Controlled_Buffer controlled_buffer_9
  assign Adr6__0 = JGRT ? 7'b0011000 : 7'bz;  // Controlled_Buffer controlled_buffer_10
  assign Adr6__0 = JLEQ ? 7'b0011000 : 7'bz;  // Controlled_Buffer controlled_buffer_11
  assign Adr6__0 = JMP ? 7'b0011001 : 7'bz;  // Controlled_Buffer controlled_buffer_12
  assign Adr6__0 = JSR ? 7'b0011010 : 7'bz;  // Controlled_Buffer controlled_buffer_13
  assign Adr6__0 = RTI ? 7'b0011111 : 7'bz;  // Controlled_Buffer controlled_buffer_14
  assign Adr6__0 = POPPSW ? 7'b0100111 : 7'bz;  // Controlled_Buffer controlled_buffer_15
  assign Adr6__0 = RTS ? 7'b0101110 : 7'bz;  // Controlled_Buffer controlled_buffer_16
  assign Adr6__0 = ROR ? 7'b0110101 : 7'bz;  // Controlled_Buffer controlled_buffer_17
  assign Adr6__0 = RORC ? 7'b0110111 : 7'bz;  // Controlled_Buffer controlled_buffer_18
  assign Adr6__0 = PUSHPSW ? 7'b0111001 : 7'bz;  // Controlled_Buffer controlled_buffer_19
  assign Adr6__0 = STIVTP ? 7'b0111110 : 7'bz;  // Controlled_Buffer controlled_buffer_20
  assign Adr6__0 = HALT ? 7'b1000000 : 7'bz;  // Controlled_Buffer controlled_buffer_21

  // Notes on the sheet:
  //   Ovo radi
endmodule

module REG6_INC_LD (
  input  [5:0] I5__0,
  input  LD,
  input  INC,
  input  mr,
  input  CLK,
  output [5:0] A5__0
);

  wire reg2m_inc_ld_1_p7, reg2m_inc_ld_2_p8;

  // REG2m_INC_LD reg2m_inc_ld_1: pin names not known; wires that end beside it: CLK, mr, I5__0[5:4], A5__0[5:4], LD, INC, reg2m_inc_ld_1_p7
  // REG2m_INC_LD reg2m_inc_ld_2: pin names not known; wires that end beside it: CLK, reg2m_inc_ld_1_p7, mr, I5__0[3:2], A5__0[3:2], LD, INC, reg2m_inc_ld_2_p8
  // REG2m_INC_LD reg2m_inc_ld_3: pin names not known; wires that end beside it: CLK, reg2m_inc_ld_2_p8, mr, I5__0[1:0], A5__0[1:0], LD, INC, INC

  // Notes on the sheet:
  //   __
endmodule

module ALU16_ADD_OR (
  input  Cin,
  input  [15:0] A,
  input  [15:0] B,
  input  add,
  input  \or ,
  output [15:0] F,
  output Cout
);

  wire adder_1_cout;
  wire [15:0] adder_1_out, or_1_out;

  Adder #(.width(16)) adder_1 (.a(A), .b(B), .out(adder_1_out), .cin(Cin), .cout(adder_1_cout));
  assign or_1_out = A | B;  // OR_Gate or_1, 16 bits wide
  assign F = add ? adder_1_out : 16'bz;  // Controlled_Buffer controlled_buffer_1
  assign Cout = add ? adder_1_cout : 1'bz;  // Controlled_Buffer controlled_buffer_2
  Pull_Resistor pull_resistor_1 (.node(Cout));
  Pull_Resistor pull_resistor_2 (.node(F));
  assign F = \or  ? or_1_out : 16'bz;  // Controlled_Buffer controlled_buffer_3
endmodule

module GPR16x16 (
  input  [15:0] DI,
  input  WR,
  input  [3:0] A3__0,
  input  CLK,
  output [15:0] DO
);

  wire L, R;
  wire [15:0] controlled_buffer_1_out, controlled_buffer_3_out, gpr8x16_1_p4, gpr8x16_2_p4;

  // DC1_2 dc1_2_1: pin names not known; wires that end beside it: A3__0[3], 1'b1, L, R
  assign controlled_buffer_1_out = L ? DI : 16'bz;  // Controlled_Buffer controlled_buffer_1
  // GPR8x16 gpr8x16_1: pin names not known; wires that end beside it: A3__0[2:0], CLK, controlled_buffer_1_out, gpr8x16_1_p4, WR
  assign DO = L ? gpr8x16_1_p4 : 16'bz;  // Controlled_Buffer controlled_buffer_2
  assign controlled_buffer_3_out = R ? DI : 16'bz;  // Controlled_Buffer controlled_buffer_3
  // GPR8x16 gpr8x16_2: pin names not known; wires that end beside it: A3__0[2:0], CLK, controlled_buffer_3_out, gpr8x16_2_p4, WR
  assign DO = R ? gpr8x16_2_p4 : 16'bz;  // Controlled_Buffer controlled_buffer_4

  // Other names for the same wires on the sheet: A2__0[2:0] = A3__0[2:0]; A3 = A3__0[3]
endmodule
