// Logisim project main.circ as structural Verilog: 8 circuits, main circuit COMPUTER
module COMPUTER (
  input  in_1
);

  wire BTN_RST_out, CLK, cpu_1_inta, interrupt_interface_4_1_p4, interrupt_interface_4_1_p5,
       interrupt_interface_4_1_p6, interrupt_interface_4_1_p7, pull_resistor_1_node, pull_resistor_5_node,
       ram_1_out_9, rst;
  wire [1:0] cpu_1_uext1__0;
  wire [3:0] interrupt_interface_4_1_p1;
  wire [7:0] pull_resistor_2_node, ram_1_out_8;
  wire [15:0] risingedge_1_p4;

  Button BTN_RST (.out(BTN_RST_out));
  Clock u_CLK (.out(CLK));
  // RisingEdge risingedge_1: pin names not known; wires that end beside it: BTN_RST_out, CLK, rst, risingedge_1_p4
  RAM ram_1 (
    .in_1(risingedge_1_p4), .in_2(CLK), .in_4(pull_resistor_2_node), .in_5(pull_resistor_1_node),
    .in_6(pull_resistor_5_node), .in_7(rst), .out_8(ram_1_out_8), .out_9(ram_1_out_9), .DEBUG(in_1));
  Pull_Resistor pull_resistor_1 (.node(pull_resistor_1_node));
  Pull_Resistor pull_resistor_2 (.node(pull_resistor_2_node));
  Pull_Resistor pull_resistor_3 (.node(ram_1_out_8));
  Pull_Resistor pull_resistor_4 (.node(ram_1_out_9));
  Pull_Resistor pull_resistor_5 (.node(pull_resistor_5_node));
  CPU cpu_1 (
    .in_1(rst), .in_2(CLK), .in_3(ram_1_out_9), .in_4(ram_1_out_8), .ABUS(risingedge_1_p4),
    .DOUTBUS(pull_resistor_2_node), .out_8(pull_resistor_1_node), .out_9(pull_resistor_5_node),
    .inta(cpu_1_inta), .intr3__0(interrupt_interface_4_1_p1), .UEXT1__0(cpu_1_uext1__0));
  // INTERRUPT_INTERFACE_4 interrupt_interface_4_1: pin names not known; wires that end beside it: interrupt_interface_4_1_p1, cpu_1_inta, cpu_1_uext1__0, interrupt_interface_4_1_p4, interrupt_interface_4_1_p5, interrupt_interface_4_1_p6, interrupt_interface_4_1_p7, CLK
  Button BTN_INTR3 (.out(interrupt_interface_4_1_p4));
  Button BTN_INTR2 (.out(interrupt_interface_4_1_p5));
  Button BTN_INTR1 (.out(interrupt_interface_4_1_p6));
  Button BTN_INTR0 (.out(interrupt_interface_4_1_p7));
endmodule

module CPU (
  input  in_1,
  input  in_2,
  input  in_3,
  input  [7:0] in_4,
  input  [3:0] intr3__0,
  output [15:0] ABUS,
  output [7:0] DOUTBUS,
  output out_8,
  output out_9,
  output inta,
  output [1:0] UEXT1__0
);

  wire exec_1_setivtp;
  wire [3:0] common_1_phaseffbus;
  wire [6:0] common_1_addrbus, pull_resistor_3_node;
  wire [7:0] pull_resistor_6_node;
  wire [14:0] pull_resistor_7_node;
  wire [15:0] A, ALU, B, INTRADDR, PSW;
  wire [19:0] pull_resistor_4_node;
  wire [22:0] common_1_instrucbus;

  COMMON common_1 (
    .CLK(in_2), .RST(in_1), .DIN(in_4), .CMEMBUS(pull_resistor_7_node), .MAR(ABUS), .MDR(DOUTBUS),
    .PHASEFFBUS(common_1_phaseffbus), .ADDRBUS(common_1_addrbus), .PSW(PSW), .CREGBUS(pull_resistor_4_node),
    .CFFBUS(pull_resistor_6_node), .B(B), .A(A), .CPSW(pull_resistor_3_node), .ALU(ALU), .IVTPPDSP(INTRADDR),
    .INSTRUCBUS(common_1_instrucbus));
  Pull_Resistor pull_resistor_1 (.node(common_1_instrucbus));
  Pull_Resistor pull_resistor_2 (.node(common_1_phaseffbus));
  Pull_Resistor pull_resistor_3 (.node(pull_resistor_3_node));
  Pull_Resistor pull_resistor_4 (.node(pull_resistor_4_node));
  Pull_Resistor pull_resistor_5 (.node(common_1_addrbus));
  Pull_Resistor pull_resistor_6 (.node(pull_resistor_6_node));
  Pull_Resistor pull_resistor_7 (.node(pull_resistor_7_node));
  FETCH fetch_1 (
    .in_1(in_1), .in_2(in_2), .in_3(in_3), .PHASEFFBUS(common_1_phaseffbus),
    .INSTRUCBUS(common_1_instrucbus), .ADDRBUS(common_1_addrbus), .PSW(PSW), .rdMEM(out_9),
    .CMEMBUS(pull_resistor_7_node), .CFFBUS(pull_resistor_6_node), .CREGBUS(pull_resistor_4_node));
  ADDR addr_1 (
    .in_1(in_1), .in_2(in_2), .in_3(in_3), .PHASEFFBUS(common_1_phaseffbus),
    .INSTRUCBUS(common_1_instrucbus), .ADDRBUS(common_1_addrbus), .rdMEM(out_9),
    .CMEMBUS(pull_resistor_7_node), .CFFBUS(pull_resistor_6_node), .CREGBUS(pull_resistor_4_node));
  EXEC exec_1 (
    .in_1(in_1), .in_2(in_2), .in_3(in_3), .B(B), .PHASEFFBUS(common_1_phaseffbus),
    .INSTRUCBUS(common_1_instrucbus), .ADDRBUS(common_1_addrbus), .PSW(PSW), .A(A), .ALU(ALU),
    .CMEMBUS(pull_resistor_7_node), .CFFBUS(pull_resistor_6_node), .CREGBUS(pull_resistor_4_node),
    .CPSW(pull_resistor_3_node), .rdMEM(out_9), .wrMEM(out_8), .setIVTP(exec_1_setivtp));
  INTR intr_1 (
    .in_1(in_1), .in_2(in_2), .in_3(in_3), .PHASEFFBUS(common_1_phaseffbus),
    .INSTRUCBUS(common_1_instrucbus), .PSW(PSW), .intr(intr3__0), .ADDIVTP(INTRADDR),
    .CMEMBUS(pull_resistor_7_node), .CFFBUS(pull_resistor_6_node), .CREGBUS(pull_resistor_4_node),
    .rdMEM(out_9), .wrMEM(out_8), .UEXT1__0(UEXT1__0), .inta(inta), .ACC(A), .in_4(exec_1_setivtp));

  // Other names for the same wires on the sheet: CLK = in_2; DIN7__0[7:0] = in_4; FCBUS = in_3; MAR[15:0] = ABUS;
  //   MDR[7:0] = DOUTBUS; RD = out_9; rst = in_1; WR = out_8
endmodule

module COMMON (
  input  CLK,
  input  RST,
  input  [7:0] DIN,
  input  [15:0] A,
  input  [15:0] ALU,
  input  [15:0] IVTPPDSP,
  input  [14:0] CMEMBUS,
  input  [7:0] CFFBUS,
  input  [19:0] CREGBUS,
  input  [6:0] CPSW,
  output [15:0] MAR,
  output [7:0] MDR,
  output [3:0] PHASEFFBUS,
  output [22:0] INSTRUCBUS,
  output [6:0] ADDRBUS,
  output [15:0] PSW,
  output [15:0] B
);

  wire ADRINST, adrinst_t, and_1_out, and_2_out, and_3_out, and_4_out, and_5_out, and_6_out, and_9_out,
       and_10_out, and_11_out, and_12_out, and_13_out, and_14_out, and_15_out, and_16_out, and_17_out,
       and_18_out, and_19_out, and_20_out, and_21_out, and_22_out, and_23_out, and_24_out, and_25_out,
       and_26_out, and_27_out, and_28_out, and_30_out, and_31_out, and_32_out, and_34_out, bezadrinst, Bis0,
       BisMININT, branchinst, changePSW, checkAddressing, gradr, grinst, IR23, IR27, jumpinst, mp2_1b_1_p3,
       mp2_16b_1_p2, mp2_16b_2_p3, mp4_16b_1_p5, mp4_16b_2_p5, mp8_8b_1_p8, mp8_8b_1_p12, mp8_16b_1_p8,
       mp8_16b_1_p12, not_1_out, not_4_out, not_9_out, or_1_out, or_2_out, or_3_out, or_4_out, or_6_out,
       or_7_out, or_8_out, or_9_out, or_12_out, or_13_out, or_14_out, or_15_out, or_16_out, or_17_out,
       or_18_out, or_19_out, or_20_out, reg16_inc_ld_1_p4, rsff_2_p4, rsff_3_p4, rsff_5_p3, rsff_5_p4,
       rsff_6_p4, rsff_7_p4, rsff_8_p3, rsff_8_p4, rsff_10_p3, rsff_10_p4, stopLoop;
  wire [0:0] IR26__24;
  wire [1:0] checkAdrInst, checkJumpInst, IR29__28;
  wire [2:0] checkBranchInst, IR22__20;
  wire [3:0] IR19__16;
  wire [7:0] IR7__0, IR15__8, xor_1_out;
  wire [7:6] IR31__24;
  wire [15:0] ADDPCREL15__0, DW15__0, GPR15__0, mp2_16b_3_p3, mp8_16b_1_p11, PC15__0, SP15__0;

  // MP8_16b mp8_16b_1: pin names not known; wires that end beside it: CMEMBUS[7], CMEMBUS[6], CMEMBUS[5], PC15__0, {IR15__8, IR7__0}, B, GPR15__0, mp8_16b_1_p8, SP15__0, IVTPPDSP, mp8_16b_1_p11, mp8_16b_1_p12, mp8_16b_1_p12, 1'b1
  // REG16 reg16_1: pin names not known; wires that end beside it: CLK, mp8_16b_1_p8, MAR, CMEMBUS[0], CMEMBUS[3], CREGBUS[14]
  // Probe on MAR
  // REG8_LD reg8_ld_1: pin names not known; wires that end beside it: CLK, MDR, {IR31__24, IR29__28, IR27, checkJumpInst, IR26__24[0]}, CREGBUS[19]
  // Probe on {IR31__24, IR29__28, IR27, checkJumpInst, IR26__24[0]}
  // DC3_8 dc3_8_1: pin names not known; wires that end beside it: {checkJumpInst, IR26__24[0]}, branchinst, INSTRUCBUS[5], INSTRUCBUS[6], INSTRUCBUS[7], INSTRUCBUS[3], INSTRUCBUS[4], checkBranchInst[0], checkBranchInst[1], checkBranchInst[2]
  // MP2_1b mp2_1b_1: pin names not known; wires that end beside it: 1'b1, PSW[4], mp2_1b_1_p3, B[0], CREGBUS[10]
  and and_1 (and_1_out, branchinst, or_1_out);
  or or_1 (or_1_out, checkBranchInst[0], checkBranchInst[1], checkBranchInst[2]);
  and and_2 (and_2_out, adrinst_t, or_2_out);
  or or_2 (or_2_out, checkAdrInst[0], checkAdrInst[1]);
  or or_3 (or_3_out, IR31__24[6], IR31__24[7]);
  or or_4 (or_4_out, checkJumpInst[0], checkJumpInst[1]);
  // MP2_16b mp2_16b_1: pin names not known; wires that end beside it: CREGBUS[0], mp2_16b_1_p2, 1'b1
  // MP4_16b mp4_16b_1: pin names not known; wires that end beside it: CREGBUS[2], CREGBUS[1], {IR15__8, IR7__0}, mp2_16b_1_p2, mp4_16b_1_p5, mp4_16b_1_p5, GPR15__0, A, 1'b1
  // REG16 reg16_2: pin names not known; wires that end beside it: CREGBUS[8], CREGBUS[9], mp2_1b_1_p3, CLK, B, CREGBUS[3], CREGBUS[4], CREGBUS[5]
  Subtractor #(.width(16)) subtractor_1 (.a(MAR), .b(16'h1), .out(mp8_16b_1_p11));  // open: bin, bout
  // DC3_8 dc3_8_2: pin names not known; wires that end beside it: {checkJumpInst, IR26__24[0]}, bezadrinst, INSTRUCBUS[8], INSTRUCBUS[9], INSTRUCBUS[10], INSTRUCBUS[11], INSTRUCBUS[12], INSTRUCBUS[13], INSTRUCBUS[14], INSTRUCBUS[15]
  or or_5 (grinst, IR27, and_1_out, and_2_out, or_3_out, and_3_out);
  and and_3 (and_3_out, jumpinst, or_4_out);
  // Probe on B
  nor nor_1 (INSTRUCBUS[0], MDR[0], MDR[1], MDR[2], MDR[3], MDR[4], MDR[5], MDR[6], MDR[7]);
  // REG8_LD reg8_ld_2: pin names not known; wires that end beside it: CLK, MDR, {IR23, IR22__20, IR19__16}, CREGBUS[18]
  // Probe on {IR23, IR22__20, IR19__16}
  // DC2_4 dc2_4_1: pin names not known; wires that end beside it: IR29__28, bezadrinst, branchinst, jumpinst, adrinst_t
  // DC3_8 dc3_8_3: pin names not known; wires that end beside it: IR22__20, adrinst_t, ADDRBUS[0], ADDRBUS[1], ADDRBUS[2], ADDRBUS[3], ADDRBUS[4], ADDRBUS[5], ADDRBUS[6], checkAddressing
  // ADD16 add16_1: pin names not known; wires that end beside it: {{9{IR23}}, IR22__20, IR19__16}, ADDPCREL15__0, PC15__0
  // REG8_LD reg8_ld_3: pin names not known; wires that end beside it: CLK, MDR, IR7__0, CREGBUS[16]
  // MP8_8b mp8_8b_1: pin names not known; wires that end beside it: CMEMBUS[10], CMEMBUS[9], CMEMBUS[8], DIN, A[15:8], A[7:0], B[15:8], mp8_8b_1_p8, B[7:0], PC15__0[15:8], PC15__0[7:0], mp8_8b_1_p12, 1'b1
  // Probe on mp8_8b_1_p8
  // REG8_LD reg8_ld_4: pin names not known; wires that end beside it: CLK, mp8_8b_1_p8, MDR, CMEMBUS[1]
  // Probe on MDR
  // Probe on IR7__0
  // DC3_8 dc3_8_4: pin names not known; wires that end beside it: {checkJumpInst, IR26__24[0]}, adrinst_t, INSTRUCBUS[16], INSTRUCBUS[17], INSTRUCBUS[18], INSTRUCBUS[19], INSTRUCBUS[20], INSTRUCBUS[21], checkAdrInst[0], checkAdrInst[1]
  // MP2_8b mp2_8b_1: pin names not known; wires that end beside it: CREGBUS[7], {PSW[15], {7{1'b0}}}, mp8_8b_1_p12, {3'b000, PSW[4:0]}, 1'b1
  // REG8_LD reg8_ld_5: pin names not known; wires that end beside it: CLK, MDR, IR15__8, CREGBUS[17]
  // Probe on IR15__8
  // DC1_2 dc1_2_1: pin names not known; wires that end beside it: IR26__24[0], jumpinst, INSTRUCBUS[1], INSTRUCBUS[2]
  or or_6 (or_6_out, IR19__16[0], IR19__16[1], IR19__16[2], IR19__16[3]);
  or or_7 (or_7_out, ADDRBUS[0], ADDRBUS[1], ADDRBUS[2]);
  or or_8 (or_8_out, INSTRUCBUS[17], INSTRUCBUS[19]);
  or or_9 (or_9_out, ADDRBUS[0], ADDRBUS[6]);
  // REG8_LD reg8_ld_6: pin names not known; wires that end beside it: CLK, MDR, DW15__0[15:8], CREGBUS[12]
  and and_4 (and_4_out, or_6_out, or_7_out);
  and and_5 (and_5_out, ADDRBUS[0], or_8_out);
  and and_6 (and_6_out, INSTRUCBUS[21], or_9_out);
  or or_10 (gradr, IR23, checkAddressing, and_4_out, and_5_out, and_6_out);
  // REG8_LD reg8_ld_7: pin names not known; wires that end beside it: CLK, MDR, DW15__0[7:0], CREGBUS[11]
  // MP4_16b mp4_16b_2: pin names not known; wires that end beside it: CMEMBUS[14], CMEMBUS[13], {IR23, IR22__20, IR19__16, IR15__8}, ADDPCREL15__0, mp4_16b_2_p5, DW15__0, 1'b1
  // REG16 reg16_3: pin names not known; wires that end beside it: CLK, 16'hf000, SP15__0, RST, CMEMBUS[11], CMEMBUS[12]
  not not_1 (not_1_out, RST);
  // RSFF rsff_1: pin names not known; wires that end beside it: CFFBUS[1], CLK, CFFBUS[0], not_1_out, PHASEFFBUS[0]
  // MP2_16b mp2_16b_2: pin names not known; wires that end beside it: RST, mp4_16b_2_p5, mp2_16b_2_p3, 16'h1000, 1'b1
  // REG16_INC_LD reg16_inc_ld_1: pin names not known; wires that end beside it: CLK, mp2_16b_2_p3, PC15__0, reg16_inc_ld_1_p4, CMEMBUS[2]
  or or_11 (reg16_inc_ld_1_p4, CMEMBUS[4], RST);
  // Probe on PC15__0
  and and_7 (BisMININT, ~B[0], ~B[1], ~B[2], ~B[3], ~B[4], ~B[5], ~B[6], ~B[7], ~B[8], ~B[9], ~B[10], ~B[11], ~B[12], ~B[13], ~B[14], B[15]);  // AND_Gate
  and and_8 (Bis0, ~B[0], ~B[1], ~B[2], ~B[3], ~B[4], ~B[5], ~B[6], ~B[7], ~B[8], ~B[9], ~B[10], ~B[11], ~B[12], ~B[13], ~B[14], ~B[15]);  // AND_Gate
  // RSFF rsff_2: pin names not known; wires that end beside it: CFFBUS[3], CLK, CFFBUS[2], rsff_2_p4, PHASEFFBUS[1]
  not not_2 (rsff_2_p4, RST);
  and and_9 (and_9_out, MDR[2], changePSW);
  and and_10 (and_10_out, ADRINST, A[15]);
  and and_11 (and_11_out, ~ALU[15], B[15], A[15]);  // AND_Gate
  or or_12 (or_12_out, and_11_out, and_12_out);
  and and_12 (and_12_out, ALU[15], ~B[15], ~A[15]);  // AND_Gate
  and and_13 (and_13_out, ~CREGBUS[15], B[15], A[15]);  // AND_Gate
  or or_13 (or_13_out, and_13_out, and_14_out);
  and and_14 (and_14_out, CREGBUS[15], ~B[15], ~A[15]);  // AND_Gate
  // RSFF rsff_3: pin names not known; wires that end beside it: CFFBUS[5], CLK, CFFBUS[4], rsff_3_p4, PHASEFFBUS[2]
  not not_3 (rsff_3_p4, RST);
  and and_15 (and_15_out, ~MDR[0], changePSW, CPSW[6]);  // AND_Gate
  and and_16 (and_16_out, MDR[0], changePSW, CPSW[6]);
  and and_17 (and_17_out, MDR[1], changePSW);
  and and_18 (and_18_out, ADRINST, and_19_out);
  and and_19 (and_19_out, ~A[0], ~A[1], ~A[2], ~A[3], ~A[4], ~A[5], ~A[6], ~A[7], ~A[8], ~A[9], ~A[10], ~A[11], ~A[12], ~A[13], ~A[14], ~A[15]);  // AND_Gate
  or or_14 (or_14_out, and_9_out, and_10_out);
  and and_20 (and_20_out, MDR[3], changePSW);
  and and_21 (and_21_out, INSTRUCBUS[18], or_12_out);
  and and_22 (and_22_out, MDR[4], changePSW);
  and and_23 (and_23_out, INSTRUCBUS[18], or_13_out);
  or or_15 (or_15_out, and_23_out, and_24_out);
  and and_24 (and_24_out, A[0], or_20_out);
  or or_16 (or_16_out, and_15_out, CPSW[0]);
  or or_17 (or_17_out, and_17_out, and_18_out);
  or or_18 (or_18_out, and_20_out, and_21_out);
  and and_25 (and_25_out, MDR[7], changePSW);
  or or_19 (or_19_out, and_22_out, or_15_out);
  or or_20 (or_20_out, INSTRUCBUS[11], INSTRUCBUS[12]);
  // MP2_16b mp2_16b_3: pin names not known; wires that end beside it: CREGBUS[13], B, mp2_16b_3_p3, A, 1'b1
  GPR16x16 gpr16x16_1 (.DI(mp2_16b_3_p3), .A3__0(IR19__16), .DO(GPR15__0), .CLK(CLK), .WR(CREGBUS[6]));
  not not_4 (not_4_out, RST);
  // RSFF rsff_4: pin names not known; wires that end beside it: or_16_out, CLK, and_16_out, not_4_out, PSW[0]
  and and_26 (and_26_out, ~or_17_out, CPSW[5]);  // AND_Gate
  and and_27 (and_27_out, or_17_out, CPSW[5]);
  and and_28 (and_28_out, ~or_14_out, CPSW[4]);  // AND_Gate
  // RSFF rsff_5: pin names not known; wires that end beside it: and_28_out, CLK, rsff_5_p3, rsff_5_p4, PSW[2]
  and and_29 (rsff_5_p3, or_14_out, CPSW[4]);
  not not_5 (rsff_5_p4, RST);
  and and_30 (and_30_out, ~and_25_out, CPSW[1]);  // AND_Gate
  and and_31 (and_31_out, and_25_out, CPSW[1]);
  assign xor_1_out = A[7:0] ^ MDR;  // XOR_Gate xor_1, 8 bits wide
  nor nor_2 (INSTRUCBUS[22], xor_1_out[7], xor_1_out[6], xor_1_out[5], xor_1_out[4], xor_1_out[3], xor_1_out[2], xor_1_out[1], xor_1_out[0]);
  // RSFF rsff_6: pin names not known; wires that end beside it: CFFBUS[7], CLK, CFFBUS[6], rsff_6_p4, PHASEFFBUS[3]
  not not_6 (rsff_6_p4, RST);
  or or_21 (ADRINST, INSTRUCBUS[16], INSTRUCBUS[18], INSTRUCBUS[20], INSTRUCBUS[21]);
  or or_22 (changePSW, INSTRUCBUS[10], INSTRUCBUS[14]);
  // RSFF rsff_7: pin names not known; wires that end beside it: and_26_out, CLK, and_27_out, rsff_7_p4, PSW[1]
  not not_7 (rsff_7_p4, RST);
  and and_32 (and_32_out, ~or_18_out, CPSW[3]);  // AND_Gate
  // RSFF rsff_8: pin names not known; wires that end beside it: and_32_out, CLK, rsff_8_p3, rsff_8_p4, PSW[3]
  and and_33 (rsff_8_p3, or_18_out, CPSW[3]);
  not not_8 (rsff_8_p4, RST);
  not not_9 (not_9_out, RST);
  // RSFF rsff_9: pin names not known; wires that end beside it: and_30_out, CLK, and_31_out, not_9_out, PSW[15]
  and and_34 (and_34_out, ~or_19_out, CPSW[2]);  // AND_Gate
  // RSFF rsff_10: pin names not known; wires that end beside it: and_34_out, CLK, rsff_10_p3, rsff_10_p4, PSW[4]
  and and_35 (rsff_10_p3, or_19_out, CPSW[2]);
  not not_10 (rsff_10_p4, RST);
  or or_23 (stopLoop, INSTRUCBUS[22], INSTRUCBUS[0]);

  assign PSW[14:5] = {10{1'b0}};

  // Other names for the same wires on the sheet: MDR7__0[7:0] = MDR; IR23__16[7:0] = {IR23, IR22__20, IR19__16};
  //   A15__0[15:0] = A; immed = ADDRBUS[0]; memdir = ADDRBUS[1]; memind = ADDRBUS[2]; regind = ADDRBUS[3];
  //   preincr = ADDRBUS[4]; postdec = ADDRBUS[5]; regdir = ADDRBUS[6]; ALU15__0[15:0] = ALU; B15__0[15:0] = B;
  //   stariji[7:0] = B[15:8]; stFETCH = CFFBUS[0]; clFETCH = CFFBUS[1]; stADDR = CFFBUS[2]; clADDR = CFFBUS[3];
  //   stEXEC = CFFBUS[4]; clEXEC = CFFBUS[5]; stINTR = CFFBUS[6]; clINTR = CFFBUS[7]; ldMAR = CMEMBUS[0];
  //   ldMDR = CMEMBUS[1]; incPC = CMEMBUS[2]; incMAR = CMEMBUS[3]; ldPC = CMEMBUS[4]; mxMAR0 = CMEMBUS[5];
  //   mxMAR1 = CMEMBUS[6]; mxMAR2 = CMEMBUS[7]; mxMDR0 = CMEMBUS[8]; mxMDR1 = CMEMBUS[9]; mxMDR2 = CMEMBUS[10];
  //   incSP = CMEMBUS[11]; decSP = CMEMBUS[12]; mxPC0 = CMEMBUS[13]; mxPC1 = CMEMBUS[14]; clPSWSTART = CPSW[0];
  //   ldI = CPSW[1]; ldC = CPSW[2]; ldV = CPSW[3]; ldN = CPSW[4]; ldZ = CPSW[5]; ldSTART = CPSW[6];
  //   mxB_MDR0 = CREGBUS[0]; mxB0 = CREGBUS[1]; mxB1 = CREGBUS[2]; ldB = CREGBUS[3]; incB = CREGBUS[4];
  //   decB = CREGBUS[5]; wrGPR = CREGBUS[6]; mx0 = CREGBUS[7]; clB = CREGBUS[8]; shrB = CREGBUS[9];
  //   mxRO0 = CREGBUS[10]; ldDWL = CREGBUS[11]; ldDWH = CREGBUS[12]; mxGPR0 = CREGBUS[13]; decMAR = CREGBUS[14];
  //   Cout = CREGBUS[15]; ldIR7__0 = CREGBUS[16]; ldIR15__8 = CREGBUS[17]; ldIR23__16 = CREGBUS[18];
  //   ldIR31__24 = CREGBUS[19]; Din7__0[7:0] = DIN; DWL7__0[7:0] = DW15__0[7:0]; DWH7__0[7:0] = DW15__0[15:8];
  //   ENTRADDR15__0[15:0] = IVTPPDSP; MDRis0 = INSTRUCBUS[0]; JMP = INSTRUCBUS[1]; JSR = INSTRUCBUS[2];
  //   JGRT = INSTRUCBUS[3]; JLEQ = INSTRUCBUS[4]; BGREU = INSTRUCBUS[5]; BLSSU = INSTRUCBUS[6]; BLEQU = INSTRUCBUS[7];
  //   HALT = INSTRUCBUS[8]; RTS = INSTRUCBUS[9]; RTI = INSTRUCBUS[10]; ROR = INSTRUCBUS[11]; RORC = INSTRUCBUS[12];
  //   PUSHPSW = INSTRUCBUS[13]; POPPSW = INSTRUCBUS[14]; STIVTP = INSTRUCBUS[15]; LD = INSTRUCBUS[16];
  //   ST = INSTRUCBUS[17]; ADD = INSTRUCBUS[18]; DEC = INSTRUCBUS[19]; OR = INSTRUCBUS[20]; STRFIND = INSTRUCBUS[21];
  //   equal = INSTRUCBUS[22]; IR31__24[5:0] = {IR29__28, IR27, checkJumpInst, IR26__24[0]};
  //   IR26__24[2:1] = checkJumpInst; IR31__30[1:0] = IR31__24; MAR15__0[15:0] = MAR; FETCH = PHASEFFBUS[0];
  //   ADDR = PHASEFFBUS[1]; EXEC = PHASEFFBUS[2]; INTR = PHASEFFBUS[3]; PSW7__0[4:0] = PSW[4:0];
  //   PSW15__0 (some bits) = {PSW[15], PSW[4:0]}; PSWSTART = PSW[0]; PSWZ = PSW[1]; PSWN = PSW[2]; PSWV = PSW[3];
  //   PSWC = PSW[4]; PSW15__8[7] = PSW[15]; PSWI = PSW[15]

  // Notes on the sheet:
  //   MAR
  //   Sabirac
  //   Sabirac
  //   Instrukcijski registar
  //   Pomocni registri
  //   IR31..24
  //   IR23..16
  //   Dekoderi za prepoznavanje instrukcije na osnovu sadrzaja registra IR31..24
  //   MDR
  //   IR7..0
  //   IR15..8
  //   SP
  //   PC
  //   FF za pokretanje FETCH, ADDR, EXEC i INTR faze izvršavanja instrukcije
  //   Registarski fajl
  //   Programska statusna reč (PSW)
endmodule

module FETCH (
  input  in_1,
  input  in_2,
  input  in_3,
  input  [3:0] PHASEFFBUS,
  input  [22:0] INSTRUCBUS,
  input  [6:0] ADDRBUS,
  input  [15:0] PSW,
  output [14:0] CMEMBUS,
  output [7:0] CFFBUS,
  output [19:0] CREGBUS,
  output rdMEM
);

  wire adr2, and_2_out, and_3_out, and_4_out, and_5_out, and_6_out, and_7_out, bezadr1, bradr2, brbezadr1,
       brcnd, brgradr, brgrinst, brjmp2, brjmp3, brnotFCBUS, bruncnd, clFETCH, incPC, jmp2, jmp3, ldIR7__0,
       ldIR15__8, ldIR23__16, ldIR31__24, ldMAR, ldMDR, not_1_out, not_3_out, not_4_out, not_5_out,
       notPSWSTARTandFETCH, or_4_out, or_5_out, or_7_out, rdMEM_t, reg5_cl_inc_ld_1_p5, reg5_cl_inc_ld_1_p6,
       stADDR, stEXEC;
  wire [4:0] reg5_cl_inc_ld_1_p4;
  wire [19:11] reg5_cl_inc_ld_1_p3;

  or or_1 (bezadr1, INSTRUCBUS[8], INSTRUCBUS[9], INSTRUCBUS[10], INSTRUCBUS[11], INSTRUCBUS[12], INSTRUCBUS[13], INSTRUCBUS[14], INSTRUCBUS[15]);
  or or_2 (jmp2, INSTRUCBUS[5], INSTRUCBUS[6], INSTRUCBUS[7]);
  not not_1 (not_1_out, in_1);
  // REG5_CL_INC_LD reg5_cl_inc_ld_1: pin names not known; wires that end beside it: in_2, not_1_out, reg5_cl_inc_ld_1_p3[19:15], reg5_cl_inc_ld_1_p4, reg5_cl_inc_ld_1_p5, reg5_cl_inc_ld_1_p6
  not not_2 (reg5_cl_inc_ld_1_p6, reg5_cl_inc_ld_1_p5);
  or or_3 (reg5_cl_inc_ld_1_p5, bruncnd, brcnd);
  or or_4 (or_4_out, INSTRUCBUS[16], INSTRUCBUS[17], INSTRUCBUS[18], INSTRUCBUS[19], INSTRUCBUS[20], INSTRUCBUS[21]);
  and and_1 (adr2, or_4_out, or_5_out);
  or or_5 (or_5_out, ADDRBUS[3], ADDRBUS[4], ADDRBUS[5], ADDRBUS[6]);
  or or_6 (jmp3, INSTRUCBUS[1], INSTRUCBUS[2], INSTRUCBUS[3], INSTRUCBUS[4]);
  ROM #(.addrWidth(5), .dataWidth(20)) rom_1 (
    .addr(reg5_cl_inc_ld_1_p4),
    .data({reg5_cl_inc_ld_1_p3, stEXEC, stADDR, clFETCH, ldIR7__0, ldIR15__8, ldIR23__16, ldIR31__24, ldMDR, rdMEM_t, incPC, ldMAR}),
    .sel(1'b1));
  // DC4_16 dc4_16_1: pin names not known; wires that end beside it: reg5_cl_inc_ld_1_p3[14:11], 1'b1, bruncnd, notPSWSTARTandFETCH, brnotFCBUS, brgrinst, brbezadr1, brgradr, brjmp2, bradr2, brjmp3
  not not_3 (not_3_out, PHASEFFBUS[0]);
  not not_4 (not_4_out, PSW[0]);
  or or_7 (or_7_out, not_3_out, not_4_out);
  not not_5 (not_5_out, in_3);
  and and_2 (and_2_out, or_7_out, notPSWSTARTandFETCH);
  and and_3 (and_3_out, brbezadr1, bezadr1);
  and and_4 (and_4_out, brjmp2, jmp2);
  and and_5 (and_5_out, bradr2, adr2);
  and and_6 (and_6_out, brjmp3, jmp3);
  and and_7 (and_7_out, brnotFCBUS, not_5_out);
  or or_8 (brcnd, and_2_out, and_3_out, and_4_out, and_5_out, and_6_out, and_7_out);
  assign CFFBUS[1] = clFETCH ? 1'b1 : 1'bz;  // Controlled_Buffer controlled_buffer_1
  assign CFFBUS[2] = stADDR ? 1'b1 : 1'bz;  // Controlled_Buffer controlled_buffer_2
  assign CFFBUS[4] = stEXEC ? 1'b1 : 1'bz;  // Controlled_Buffer controlled_buffer_3
  assign CREGBUS[16] = ldIR7__0 ? 1'b1 : 1'bz;  // Controlled_Buffer controlled_buffer_4
  assign CREGBUS[17] = ldIR15__8 ? 1'b1 : 1'bz;  // Controlled_Buffer controlled_buffer_5
  assign CREGBUS[18] = ldIR23__16 ? 1'b1 : 1'bz;  // Controlled_Buffer controlled_buffer_6
  assign CREGBUS[19] = ldIR31__24 ? 1'b1 : 1'bz;  // Controlled_Buffer controlled_buffer_7
  assign CMEMBUS[0] = ldMAR ? 1'b1 : 1'bz;  // Controlled_Buffer controlled_buffer_8
  assign CMEMBUS[1] = ldMDR ? 1'b1 : 1'bz;  // Controlled_Buffer controlled_buffer_9
  assign CMEMBUS[2] = incPC ? 1'b1 : 1'bz;  // Controlled_Buffer controlled_buffer_10
  assign rdMEM = rdMEM_t ? 1'b1 : 1'bz;  // Controlled_Buffer controlled_buffer_11

  // Other names for the same wires on the sheet: immed = ADDRBUS[0]; memdir = ADDRBUS[1]; memind = ADDRBUS[2];
  //   regind = ADDRBUS[3]; preincr = ADDRBUS[4]; postdec = ADDRBUS[5]; regdir = ADDRBUS[6]; CLK = in_2; FCBUS = in_3;
  //   JMP = INSTRUCBUS[1]; JSR = INSTRUCBUS[2]; JGRT = INSTRUCBUS[3]; JLEQ = INSTRUCBUS[4]; BGREU = INSTRUCBUS[5];
  //   BLSSU = INSTRUCBUS[6]; BLEQU = INSTRUCBUS[7]; HALT = INSTRUCBUS[8]; RTS = INSTRUCBUS[9]; RTI = INSTRUCBUS[10];
  //   ROR = INSTRUCBUS[11]; RORC = INSTRUCBUS[12]; PUSHPSW = INSTRUCBUS[13]; POPPSW = INSTRUCBUS[14];
  //   STIVTP = INSTRUCBUS[15]; LD = INSTRUCBUS[16]; ST = INSTRUCBUS[17]; ADD = INSTRUCBUS[18]; DEC = INSTRUCBUS[19];
  //   OR = INSTRUCBUS[20]; STRFIND = INSTRUCBUS[21]; FETCH = PHASEFFBUS[0]; ADDR = PHASEFFBUS[1];
  //   EXEC = PHASEFFBUS[2]; INTR = PHASEFFBUS[3]; PSW15__0[15:0] = PSW; PSWSTART = PSW[0]; rst = in_1

  // Notes on the sheet:
  //   Operaciona jedinica
  //   Kontrolna jedinica
  //   contents of rom_1 (hex, n*v repeats v):
  //   1000 3 1180c 10 2000 9a800 3 3980c 20 3000 9b800 94000 3 6980c 9c840 3 8180c 80 b00 d00
endmodule

module ADDR (
  input  in_1,
  input  in_2,
  input  in_3,
  input  [3:0] PHASEFFBUS,
  input  [22:0] INSTRUCBUS,
  input  [6:0] ADDRBUS,
  output [14:0] CMEMBUS,
  output [7:0] CFFBUS,
  output [19:0] CREGBUS,
  output rdMEM
);

  wire and_1_out, and_2_out, and_3_out, bradr, brcnd, brnotADDR, brnotFCBUS, brST_STRFIND, bruncnd, clADDR,
       decB, incB, incMAR, ldB, ldMAR, ldMDR, mxB0, mxB1, mxB_MDR0, mxMAR0, mxMAR1, not_1_out, not_3_out,
       not_4_out, or_2_out, rdMEM_t, reg5_cl_inc_ld_1_p6, reg5_cl_inc_ld_1_p7, stEXEC, wrGPR;
  wire [2:0] rom_1_data;
  wire [4:0] kmadr_1_adr4__0, multiplexer_1_out, reg5_cl_inc_ld_1_p5;
  wire [22:18] rom_1_data_2;

  KMADR kmadr_1 (
    .immed(ADDRBUS[0]), .memdir(ADDRBUS[1]), .memind(ADDRBUS[2]), .regind(ADDRBUS[3]), .preincr(ADDRBUS[4]),
    .postdec(ADDRBUS[5]), .regdir(ADDRBUS[6]), .Adr4__0(kmadr_1_adr4__0));
  Multiplexer #(.width(5), .enable("false")) multiplexer_1 (
    .in0(rom_1_data_2), .in1(kmadr_1_adr4__0), .out(multiplexer_1_out), .sel(bradr));
  not not_1 (not_1_out, in_1);
  // REG5_CL_INC_LD reg5_cl_inc_ld_1: pin names not known; wires that end beside it: 1'b0, in_2, not_1_out, multiplexer_1_out, reg5_cl_inc_ld_1_p5, reg5_cl_inc_ld_1_p6, reg5_cl_inc_ld_1_p7
  not not_2 (reg5_cl_inc_ld_1_p7, reg5_cl_inc_ld_1_p6);
  or or_1 (reg5_cl_inc_ld_1_p6, bruncnd, brcnd, bradr);
  ROM #(.addrWidth(5), .dataWidth(23)) rom_1 (
    .addr(reg5_cl_inc_ld_1_p5),
    .data({rom_1_data_2, rom_1_data, stEXEC, clADDR, decB, wrGPR, incB, mxB1, mxMAR1, mxB_MDR0, incMAR, mxB0, ldMDR, rdMEM_t, mxMAR0, ldMAR, ldB}),
    .sel(1'b1));
  // DC3_8 dc3_8_1: pin names not known; wires that end beside it: rom_1_data, 1'b1, bruncnd, brnotADDR, bradr, brnotFCBUS, brST_STRFIND
  not not_3 (not_3_out, PHASEFFBUS[1]);
  or or_2 (or_2_out, INSTRUCBUS[17], INSTRUCBUS[21]);
  not not_4 (not_4_out, in_3);
  and and_1 (and_1_out, not_3_out, brnotADDR);
  and and_2 (and_2_out, or_2_out, brST_STRFIND);
  and and_3 (and_3_out, brnotFCBUS, not_4_out);
  or or_3 (brcnd, and_1_out, and_2_out, and_3_out);
  assign CMEMBUS[0] = ldMAR ? 1'b1 : 1'bz;  // Controlled_Buffer controlled_buffer_1
  assign CMEMBUS[1] = ldMDR ? 1'b1 : 1'bz;  // Controlled_Buffer controlled_buffer_2
  assign CMEMBUS[3] = incMAR ? 1'b1 : 1'bz;  // Controlled_Buffer controlled_buffer_3
  assign CMEMBUS[5] = mxMAR0 ? 1'b1 : 1'bz;  // Controlled_Buffer controlled_buffer_4
  assign CMEMBUS[6] = mxMAR1 ? 1'b1 : 1'bz;  // Controlled_Buffer controlled_buffer_5
  assign CREGBUS[0] = mxB_MDR0 ? 1'b1 : 1'bz;  // Controlled_Buffer controlled_buffer_6
  assign CREGBUS[1] = mxB0 ? 1'b1 : 1'bz;  // Controlled_Buffer controlled_buffer_7
  assign CREGBUS[2] = mxB1 ? 1'b1 : 1'bz;  // Controlled_Buffer controlled_buffer_8
  assign CREGBUS[3] = ldB ? 1'b1 : 1'bz;  // Controlled_Buffer controlled_buffer_9
  assign CREGBUS[4] = incB ? 1'b1 : 1'bz;  // Controlled_Buffer controlled_buffer_10
  assign CREGBUS[5] = decB ? 1'b1 : 1'bz;  // Controlled_Buffer controlled_buffer_11
  assign CREGBUS[6] = wrGPR ? 1'b1 : 1'bz;  // Controlled_Buffer controlled_buffer_12
  assign CFFBUS[3] = clADDR ? 1'b1 : 1'bz;  // Controlled_Buffer controlled_buffer_13
  assign CFFBUS[4] = stEXEC ? 1'b1 : 1'bz;  // Controlled_Buffer controlled_buffer_14
  assign rdMEM = rdMEM_t ? 1'b1 : 1'bz;  // Controlled_Buffer controlled_buffer_15

  // Other names for the same wires on the sheet: immed = ADDRBUS[0]; memdir = ADDRBUS[1]; memind = ADDRBUS[2];
  //   regind = ADDRBUS[3]; preincr = ADDRBUS[4]; postdec = ADDRBUS[5]; regdir = ADDRBUS[6]; CLK = in_2; FCBUS = in_3;
  //   ST = INSTRUCBUS[17]; STRFIND = INSTRUCBUS[21]; ADDR = PHASEFFBUS[1]; rst = in_1

  // Notes on the sheet:
  //   Operaciona jedinica
  //   Upravljacka jedinica
  //   contents of rom_1 (hex, n*v repeats v):
  //   10000 18000 688001 548006 6 160018 61 1e0018 a1 548102 548106 201 400 400 548902 307 1000 1000
  //   548800 6a8000 688201 6a8000 5a0018 61 620018 6880a1 e000
endmodule

module EXEC (
  input  in_1,
  input  in_2,
  input  in_3,
  input  [15:0] B,
  input  [3:0] PHASEFFBUS,
  input  [22:0] INSTRUCBUS,
  input  [6:0] ADDRBUS,
  input  [15:0] PSW,
  output [15:0] A,
  output [15:0] ALU,
  output [14:0] CMEMBUS,
  output [7:0] CFFBUS,
  output [19:0] CREGBUS,
  output setIVTP,
  output [6:0] CPSW,
  output rdMEM,
  output wrMEM
);

  wire add_t, and_1_out, and_2_out, and_3_out, and_4_out, and_5_out, and_6_out, and_7_out, and_8_out,
       and_9_out, and_10_out, and_11_out, and_12_out, brbrorjmp, brcnd, brmul, brnotEXEC, brnotFCBUS,
       brnotStopLoop, brorjmp, brPOPPSW, brregdir, bruncd, clB, clEXEC, clPSWSTART, Cout, decB, decMAR,
       decSP, incB, incMAR, incSP, ldA, ldB, ldC, ldDWH, ldDWL, ldI, ldMAR, ldMDR, ldN, ldPC, ldSTART, ldV,
       ldZ, mp4_16b_1_p2, mp4_16b_1_p7, mp4_16b_1_p9, mx0, mxA0, mxA1, mxB0, mxB1, mxMAR2, mxMDR0, mxMDR1,
       mxMDR2, mxPC0, mxPC1, mxRO0, not_1_out, not_2_out, not_3_out, not_4_out, or_1_out, or_2_out, or_3_out,
       or_t, rdMEM_t, shrB, stINTR, stopLoop, wrGPR, wrMEM_t, xor_1_out;
  wire [6:0] counter_1_q, kmopr_1_adr6__0, multiplexer_1_out;
  wire [15:0] DW15__0, subtractor_1_out;
  wire [31:21] dc4_16_1_p1;

  // MP4_16b mp4_16b_1: pin names not known; wires that end beside it: mxA1, mp4_16b_1_p2, mxA0, mp4_16b_1_p2, B, ALU, mp4_16b_1_p7, DW15__0, mp4_16b_1_p9, 1'b1
  not not_1 (not_1_out, in_1);
  // REG16_LD reg16_ld_1: pin names not known; wires that end beside it: in_2, not_1_out, mp4_16b_1_p7, A, ldA
  or or_1 (or_1_out, bruncd, brcnd, brmul);
  // DC4_16 dc4_16_1: pin names not known; wires that end beside it: dc4_16_1_p1[24:21], bruncd, brnotEXEC, brmul, brregdir, brnotFCBUS, brnotStopLoop, brbrorjmp, brPOPPSW
  Subtractor #(.width(16)) subtractor_1 (.a(B), .b(16'h1), .out(subtractor_1_out));  // open: bin, bout
  and and_1 (and_1_out, INSTRUCBUS[0], ~INSTRUCBUS[22]);  // AND_Gate
  not not_2 (not_2_out, or_1_out);
  // MP2_16b mp2_16b_1: pin names not known; wires that end beside it: and_1_out, subtractor_1_out, mp4_16b_1_p9, {16{1'b1}}, 1'b1
  Multiplexer #(.width(7), .enable("false")) multiplexer_1 (
    .in0(dc4_16_1_p1[31:25]), .in1(kmopr_1_adr6__0), .out(multiplexer_1_out), .sel(brmul));
  Counter #(.width(7), .max('h7f)) counter_1 (
    .load(or_1_out), .D(multiplexer_1_out), .count(not_2_out), .Q(counter_1_q), .clk(in_2), .clr(in_1));  // open: carry
  ALU16_ADD_OR alu16_add_or_1 (.Cin(1'b0), .A(A), .B(B), .add(add_t), .\or (or_t), .F(ALU), .Cout(Cout));
  ROM #(.addrWidth(7), .dataWidth(32)) rom_1 (
    .addr(counter_1_q),
    .data({dc4_16_1_p1, clEXEC, stINTR, clPSWSTART, setIVTP, mx0, mxRO0, shrB, mxPC1, ldSTART, ldI, ldDWL, ldDWH, incSP, decSP, ldMAR, mxMAR2, ldPC, mxPC0, mxA1, incB, rdMEM_t}));  // open: sel
  ROM #(.addrWidth(7), .dataWidth(21)) rom_2 (
    .addr(counter_1_q),
    .data({clB, or_t, wrGPR, incMAR, mxMDR2, wrMEM_t, ldMDR, mxMDR1, mxMDR0, decMAR, decB, ldC, ldV, add_t, mxA0, mxB1, mxB0, ldB, ldZ, ldN, ldA}));  // open: sel
  and and_2 (and_2_out, ~PSW[4], INSTRUCBUS[5]);  // AND_Gate
  and and_3 (and_3_out, PSW[4], INSTRUCBUS[6]);
  or or_2 (or_2_out, PSW[1], PSW[4]);
  or or_3 (or_3_out, PSW[1], xor_1_out);
  xor xor_1 (xor_1_out, PSW[2], PSW[3]);
  and and_4 (and_4_out, ~or_3_out, INSTRUCBUS[3]);  // AND_Gate
  and and_5 (and_5_out, or_3_out, INSTRUCBUS[4]);
  and and_6 (and_6_out, or_2_out, INSTRUCBUS[7]);
  KMOPR kmopr_1 (
    .LD(INSTRUCBUS[16]), .ST(INSTRUCBUS[17]), .ADD(INSTRUCBUS[18]), .DEC(INSTRUCBUS[19]),
    .OR(INSTRUCBUS[20]), .STRFIND(INSTRUCBUS[21]), .BGREU(INSTRUCBUS[5]), .BLSSU(INSTRUCBUS[6]),
    .BLEQU(INSTRUCBUS[7]), .JGRT(INSTRUCBUS[3]), .JLEQ(INSTRUCBUS[4]), .Adr6__0(kmopr_1_adr6__0),
    .JSR(INSTRUCBUS[2]), .RTI(INSTRUCBUS[10]), .POPPSW(INSTRUCBUS[14]), .JMP(INSTRUCBUS[1]),
    .ROR(INSTRUCBUS[11]), .RORC(INSTRUCBUS[12]), .PUSHPSW(INSTRUCBUS[13]), .STIVTP(INSTRUCBUS[15]),
    .HALT(INSTRUCBUS[8]), .RTS(INSTRUCBUS[9]));
  or or_4 (brorjmp, and_2_out, and_3_out, and_6_out, and_4_out, and_5_out);
  not not_3 (not_3_out, PHASEFFBUS[2]);
  and and_7 (and_7_out, brnotStopLoop, ~stopLoop);  // AND_Gate
  not not_4 (not_4_out, in_3);
  and and_8 (and_8_out, brPOPPSW, INSTRUCBUS[14]);
  and and_9 (and_9_out, not_3_out, brnotEXEC);
  and and_10 (and_10_out, ADDRBUS[6], brregdir);
  and and_11 (and_11_out, brorjmp, brbrorjmp);
  and and_12 (and_12_out, not_4_out, brnotFCBUS);
  or or_5 (brcnd, and_8_out, and_9_out, and_7_out, and_10_out, and_11_out, and_12_out);
  or or_6 (stopLoop, INSTRUCBUS[22], INSTRUCBUS[0]);
  assign CREGBUS[1] = mxB0 ? 1'b1 : 1'bz;  // Controlled_Buffer controlled_buffer_1
  assign CREGBUS[2] = mxB1 ? 1'b1 : 1'bz;  // Controlled_Buffer controlled_buffer_2
  assign CREGBUS[3] = ldB ? 1'b1 : 1'bz;  // Controlled_Buffer controlled_buffer_3
  assign CREGBUS[4] = incB ? 1'b1 : 1'bz;  // Controlled_Buffer controlled_buffer_4
  assign CREGBUS[5] = decB ? 1'b1 : 1'bz;  // Controlled_Buffer controlled_buffer_5
  assign CREGBUS[6] = wrGPR ? 1'b1 : 1'bz;  // Controlled_Buffer controlled_buffer_6
  assign CREGBUS[7] = mx0 ? 1'b1 : 1'bz;  // Controlled_Buffer controlled_buffer_7
  assign CREGBUS[8] = clB ? 1'b1 : 1'bz;  // Controlled_Buffer controlled_buffer_8
  assign CREGBUS[9] = shrB ? 1'b1 : 1'bz;  // Controlled_Buffer controlled_buffer_9
  assign CREGBUS[10] = mxRO0 ? 1'b1 : 1'bz;  // Controlled_Buffer controlled_buffer_10
  assign CREGBUS[11] = ldDWL ? 1'b1 : 1'bz;  // Controlled_Buffer controlled_buffer_11
  assign CREGBUS[12] = ldDWH ? 1'b1 : 1'bz;  // Controlled_Buffer controlled_buffer_12
  assign CMEMBUS[0] = ldMAR ? 1'b1 : 1'bz;  // Controlled_Buffer controlled_buffer_13
  assign CMEMBUS[1] = ldMDR ? 1'b1 : 1'bz;  // Controlled_Buffer controlled_buffer_14
  assign CMEMBUS[3] = incMAR ? 1'b1 : 1'bz;  // Controlled_Buffer controlled_buffer_15
  assign CMEMBUS[4] = ldPC ? 1'b1 : 1'bz;  // Controlled_Buffer controlled_buffer_16
  assign CMEMBUS[7] = mxMAR2 ? 1'b1 : 1'bz;  // Controlled_Buffer controlled_buffer_17
  assign CMEMBUS[8] = mxMDR0 ? 1'b1 : 1'bz;  // Controlled_Buffer controlled_buffer_18
  assign CMEMBUS[9] = mxMDR1 ? 1'b1 : 1'bz;  // Controlled_Buffer controlled_buffer_19
  assign CMEMBUS[10] = mxMDR2 ? 1'b1 : 1'bz;  // Controlled_Buffer controlled_buffer_20
  assign CMEMBUS[11] = incSP ? 1'b1 : 1'bz;  // Controlled_Buffer controlled_buffer_21
  assign CMEMBUS[12] = decSP ? 1'b1 : 1'bz;  // Controlled_Buffer controlled_buffer_22
  assign CMEMBUS[13] = mxPC0 ? 1'b1 : 1'bz;  // Controlled_Buffer controlled_buffer_23
  assign CMEMBUS[14] = mxPC1 ? 1'b1 : 1'bz;  // Controlled_Buffer controlled_buffer_24
  assign CPSW[0] = clPSWSTART ? 1'b1 : 1'bz;  // Controlled_Buffer controlled_buffer_25
  assign CPSW[1] = ldI ? 1'b1 : 1'bz;  // Controlled_Buffer controlled_buffer_26
  assign CPSW[2] = ldC ? 1'b1 : 1'bz;  // Controlled_Buffer controlled_buffer_27
  assign CPSW[3] = ldV ? 1'b1 : 1'bz;  // Controlled_Buffer controlled_buffer_28
  assign CPSW[4] = ldN ? 1'b1 : 1'bz;  // Controlled_Buffer controlled_buffer_29
  assign CPSW[5] = ldZ ? 1'b1 : 1'bz;  // Controlled_Buffer controlled_buffer_30
  assign CPSW[6] = ldSTART ? 1'b1 : 1'bz;  // Controlled_Buffer controlled_buffer_31
  assign CREGBUS[14] = decMAR ? 1'b1 : 1'bz;  // Controlled_Buffer controlled_buffer_32
  assign CFFBUS[5] = clEXEC ? 1'b1 : 1'bz;  // Controlled_Buffer controlled_buffer_33
  assign CFFBUS[6] = stINTR ? 1'b1 : 1'bz;  // Controlled_Buffer controlled_buffer_34
  assign CREGBUS[15] = Cout ? 1'b1 : 1'bz;  // Controlled_Buffer controlled_buffer_35
  assign rdMEM = rdMEM_t ? 1'b1 : 1'bz;  // Controlled_Buffer controlled_buffer_36
  assign wrMEM = wrMEM_t ? 1'b1 : 1'bz;  // Controlled_Buffer controlled_buffer_37

  // Other names for the same wires on the sheet: ldIVTP = setIVTP; A15__0[15:0] = A; immed = ADDRBUS[0];
  //   regdir = ADDRBUS[6]; ALU15__0[15:0] = ALU; B15__0[15:0] = B; CLK = in_2; FCBUS = in_3; MDRis0 = INSTRUCBUS[0];
  //   JMP = INSTRUCBUS[1]; JSR = INSTRUCBUS[2]; JGRT = INSTRUCBUS[3]; JLEQ = INSTRUCBUS[4]; BGREU = INSTRUCBUS[5];
  //   BLSSU = INSTRUCBUS[6]; BLEQU = INSTRUCBUS[7]; HALT = INSTRUCBUS[8]; RTS = INSTRUCBUS[9]; RTI = INSTRUCBUS[10];
  //   ROR = INSTRUCBUS[11]; RORC = INSTRUCBUS[12]; PUSHPSW = INSTRUCBUS[13]; POPPSW = INSTRUCBUS[14];
  //   STIVTP = INSTRUCBUS[15]; LD = INSTRUCBUS[16]; ST = INSTRUCBUS[17]; ADD = INSTRUCBUS[18]; DEC = INSTRUCBUS[19];
  //   OR = INSTRUCBUS[20]; STRFIND = INSTRUCBUS[21]; equal = INSTRUCBUS[22]; EXEC = PHASEFFBUS[2]; PSWSTART = PSW[0];
  //   PSWZ = PSW[1]; PSWN = PSW[2]; PSWV = PSW[3]; PSWC = PSW[4]; PSWI = PSW[15]; rst = in_1

  // Notes on the sheet:
  //   Operaciona jedinica
  //   Akumulator
  //   ALU
  //   contents of rom_1 (hex, n*v repeats v):
  //   400000 600000 0 82200000 10200000 0 82200000 0 1c800000 0 14a00000 0 18a00000 82200000 82200000 0
  //   82200000 0 24a00001 24c00002 4 82200000 82e00000 82200018 82e00000 82200010 e0 36a00000 e0 3aa00000
  //   82200010 100 160 42a00001 200 60 48a00001 400 4 100 160 52a00001 800 60 58a00001 83001000 100 160
  //   60a00001 260 64a00001 400 82202010 4000 82200000 c000 82200000 100e0 74a00000 e0 78a00000 82200000
  //   20000 82200000 40000 380000
  //   contents of rom_2 (hex, n*v repeats v):
  //   0 0 1 6 38 3c1 6 c00 0 7000 8000 34000 8000 0 40000 80041 6 100000 4000 20000 41 6 4*0 16000 8000
  //   15000 8000 0 0 0 4000 0 0 4000 0 1 0 0 4000 0 0 4000 306 0 0 4000 0 4000 0 0 200 1 200 1 17000 8000
  //   17000 8000
endmodule

module INTR (
  input  in_1,
  input  in_2,
  input  in_3,
  input  in_4,
  input  [3:0] PHASEFFBUS,
  input  [22:0] INSTRUCBUS,
  input  [15:0] PSW,
  input  [3:0] intr,
  input  [15:0] ACC,
  output [15:0] ADDIVTP,
  output [1:0] UEXT1__0,
  output inta,
  output [14:0] CMEMBUS,
  output [7:0] CFFBUS,
  output [19:0] CREGBUS,
  output rdMEM,
  output wrMEM
);

  wire and_2_out, and_3_out, and_4_out, brcnd, brnotFCBUS, brnotINTR, brnotprekid, bruncnd, clINTR, decSP,
       incMAR, ldDWH, ldDWL, ldMAR, ldMDR, ldPC, mx0, mxMAR0, mxMAR2, mxMDR0, mxMDR1, mxMDR2, mxPC1,
       not_1_out, not_2_out, not_3_out, not_5_out, not_6_out, not_7_out, prekid, prper, rdMEM_t,
       reg5_cl_inc_ld_1_p5, reg5_cl_inc_ld_1_p6, stFETCH, wrMEM_t;
  wire [2:0] dc3_8_1_p1;
  wire [2:1] IVTDSP15__0;
  wire [4:0] reg5_cl_inc_ld_1_p3, reg5_cl_inc_ld_1_p4;
  wire [15:0] IVTP15__0;

  and and_1 (prekid, prper, PSW[15], not_2_out);
  not not_1 (not_1_out, in_1);
  // REG5_CL_INC_LD reg5_cl_inc_ld_1: pin names not known; wires that end beside it: in_2, not_1_out, reg5_cl_inc_ld_1_p3, reg5_cl_inc_ld_1_p4, reg5_cl_inc_ld_1_p5, reg5_cl_inc_ld_1_p6
  // DC3_8 dc3_8_1: pin names not known; wires that end beside it: dc3_8_1_p1, 1'b1, bruncnd, brnotINTR, brnotprekid, brnotFCBUS
  not not_2 (not_2_out, INSTRUCBUS[8]);
  not not_3 (not_3_out, in_1);
  // REG16_LD reg16_ld_1: pin names not known; wires that end beside it: in_2, not_3_out, ACC, IVTP15__0, in_4
  not not_4 (reg5_cl_inc_ld_1_p6, reg5_cl_inc_ld_1_p5);
  or or_1 (prper, intr[3], intr[2], intr[1], intr[0]);
  or or_2 (reg5_cl_inc_ld_1_p5, bruncnd, brcnd);
  ROM #(.addrWidth(5), .dataWidth(27)) rom_1 (
    .addr(reg5_cl_inc_ld_1_p4),
    .data({reg5_cl_inc_ld_1_p3, dc3_8_1_p1, clINTR, stFETCH, ldPC, mxPC1, ldDWH, ldDWL, incMAR, rdMEM_t, mxMAR0, inta, mx0, mxMDR0, wrMEM_t, decSP, ldMDR, mxMDR1, mxMDR2, ldMAR, mxMAR2}));  // open: sel
  // CD4 cd4_1: pin names not known; wires that end beside it: intr[3], intr[2], intr[1], intr[0], 1'b1, UEXT1__0[1], UEXT1__0[0]
  // REG2_LD reg2_ld_1: pin names not known; wires that end beside it: in_2, UEXT1__0, IVTDSP15__0, inta
  // ADD16 add16_1: pin names not known; wires that end beside it: IVTP15__0, ADDIVTP, {{13{1'b0}}, IVTDSP15__0, 1'b0}, 1'b0
  not not_5 (not_5_out, PHASEFFBUS[3]);
  not not_6 (not_6_out, prekid);
  not not_7 (not_7_out, in_3);
  and and_2 (and_2_out, not_5_out, brnotINTR);
  and and_3 (and_3_out, not_6_out, brnotprekid);
  and and_4 (and_4_out, not_7_out, brnotFCBUS);
  or or_3 (brcnd, and_2_out, and_3_out, and_4_out);
  assign CMEMBUS[0] = ldMAR ? 1'b1 : 1'bz;  // Controlled_Buffer controlled_buffer_1
  assign CMEMBUS[1] = ldMDR ? 1'b1 : 1'bz;  // Controlled_Buffer controlled_buffer_2
  assign CMEMBUS[3] = incMAR ? 1'b1 : 1'bz;  // Controlled_Buffer controlled_buffer_3
  assign CMEMBUS[4] = ldPC ? 1'b1 : 1'bz;  // Controlled_Buffer controlled_buffer_4
  assign CMEMBUS[5] = mxMAR0 ? 1'b1 : 1'bz;  // Controlled_Buffer controlled_buffer_5
  assign CMEMBUS[7] = mxMAR2 ? 1'b1 : 1'bz;  // Controlled_Buffer controlled_buffer_6
  assign CMEMBUS[8] = mxMDR0 ? 1'b1 : 1'bz;  // Controlled_Buffer controlled_buffer_7
  assign CMEMBUS[9] = mxMDR1 ? 1'b1 : 1'bz;  // Controlled_Buffer controlled_buffer_8
  assign CMEMBUS[10] = mxMDR2 ? 1'b1 : 1'bz;  // Controlled_Buffer controlled_buffer_9
  assign CMEMBUS[12] = decSP ? 1'b1 : 1'bz;  // Controlled_Buffer controlled_buffer_10
  assign CMEMBUS[14] = mxPC1 ? 1'b1 : 1'bz;  // Controlled_Buffer controlled_buffer_11
  assign CFFBUS[0] = stFETCH ? 1'b1 : 1'bz;  // Controlled_Buffer controlled_buffer_12
  assign CFFBUS[7] = clINTR ? 1'b1 : 1'bz;  // Controlled_Buffer controlled_buffer_13
  assign CREGBUS[7] = mx0 ? 1'b1 : 1'bz;  // Controlled_Buffer controlled_buffer_14
  assign CREGBUS[11] = ldDWL ? 1'b1 : 1'bz;  // Controlled_Buffer controlled_buffer_15
  assign CREGBUS[12] = ldDWH ? 1'b1 : 1'bz;  // Controlled_Buffer controlled_buffer_16
  assign rdMEM = rdMEM_t ? 1'b1 : 1'bz;  // Controlled_Buffer controlled_buffer_17
  assign wrMEM = wrMEM_t ? 1'b1 : 1'bz;  // Controlled_Buffer controlled_buffer_18

  // Other names for the same wires on the sheet: ldBR = inta; ADDIVTP15__0[15:0] = ADDIVTP; CLK = in_2; FCBUS = in_3;
  //   HALT = INSTRUCBUS[8]; intr3__0[3:0] = intr; ldIVTP = in_4; INTR_t = PHASEFFBUS[3]; PSWI = PSW[15]; rst = in_1

  // Notes on the sheet:
  //   Operaciona jedinica
  //   Upravljacka jedinica
  //   contents of rom_1 (hex, n*v repeats v):
  //   100000 5580000 3f e00040 b7 1600040 1bf 1e00040 bf 2600040 2b 2e00040 a3 3600040 200 403 4200810
  //   3000 4a00810 4000 18000 e0000
endmodule

module RAM (
  input  [15:0] in_1,
  input  in_2,
  input  DEBUG,
  input  [7:0] in_4,
  input  in_5,
  input  in_6,
  input  in_7,
  output [7:0] out_8,
  output out_9
);

  wire and_1_out, and_2_out, CNT0, fc, LDCNT, not_1_out, notCNT0, or_1_out, reg4_ld_sl_sr_1_p6, rsff_2_p4,
       rsff_2_p5, rsff_3_p4, sl;
  wire [3:0] CNT, LFSR;

  // RSFF rsff_1: pin names not known; wires that end beside it: 1'b0, in_2, in_7, sl
  or or_1 (or_1_out, in_5, in_6);
  // REG4_LD_SL_SR reg4_ld_sl_sr_1: pin names not known; wires that end beside it: 1'b0, 1'b0, in_2, 4'b1111, LFSR, reg4_ld_sl_sr_1_p6, sl, in_7
  // RisingEdge risingedge_1: pin names not known; wires that end beside it: or_1_out, in_2, LDCNT
  // MEM64Kx8 mem64kx8_1: pin names not known; wires that end beside it: in_1, 1'b1, in_2, in_4, out_8, in_5
  xor xor_1 (reg4_ld_sl_sr_1_p6, LFSR[2], LFSR[3]);
  and and_1 (and_1_out, CNT0, not_1_out);
  not not_1 (not_1_out, LDCNT);
  // RSFF rsff_2: pin names not known; wires that end beside it: and_1_out, in_2, LDCNT, rsff_2_p4, rsff_2_p5
  not not_2 (rsff_2_p4, in_7);
  or or_2 (out_9, fc, DEBUG);
  and and_2 (and_2_out, rsff_2_p5, CNT0);
  // REG4m_DEC_LD reg4m_dec_ld_1: pin names not known; wires that end beside it: in_2, LFSR, CNT, LDCNT, notCNT0, notCNT0
  or or_3 (notCNT0, CNT[0], CNT[1], CNT[2], CNT[3]);
  // RSFF rsff_3: pin names not known; wires that end beside it: fc, in_2, and_2_out, rsff_3_p4, fc
  not not_3 (rsff_3_p4, in_7);
  not not_4 (CNT0, notCNT0);

  // Other names for the same wires on the sheet: ADR[15:0] = in_1; CLK = in_2; DIN[7:0] = in_4; DOUT[7:0] = out_8;
  //   RDMEM = in_6; rst = in_7; WRMEM = in_5

  // Notes on the sheet:
  //   Random broj predstavlja vreme pristupa memoriji
  //   Brojac za generisanje random broja 
  //   Jedinica za generisanje function complete (fc) signala
  //   Brojac za dekrementiranje random broja
endmodule
